// Logisim project 2кр_Албахтин.circ as structural Verilog: 1 circuit, main circuit main
module main (
);

  wire and_1_out, and_2_out, and_3_out, and_4_out, and_5_out, and_6_out, and_7_out, and_8_out, and_9_out,
       and_10_out, and_11_out, and_12_out, clock_1_out, or_1_out, or_2_out, or_3_out;
  wire [3:0] t_ff_4_q, t_ff_4_qn;

  Clock clock_1 (.out(clock_1_out));
  T_Flip_Flop t_ff_1 (.clk(clock_1_out), .T(or_1_out), .Q(t_ff_4_q[3]), .Qn(t_ff_4_qn[3]));  // open: preset, reset, en
  or or_1 (or_1_out, and_1_out, and_2_out, and_3_out);
  T_Flip_Flop t_ff_2 (.clk(clock_1_out), .T(or_2_out), .Q(t_ff_4_q[2]), .Qn(t_ff_4_qn[2]));  // open: preset, reset, en
  and and_1 (and_1_out, t_ff_4_qn[3], t_ff_4_qn[2]);
  and and_2 (and_2_out, t_ff_4_q[3], t_ff_4_q[2], t_ff_4_q[0]);
  and and_3 (and_3_out, t_ff_4_qn[3], t_ff_4_qn[1], t_ff_4_qn[0]);
  T_Flip_Flop t_ff_3 (.clk(clock_1_out), .T(or_3_out), .Q(t_ff_4_q[1]), .Qn(t_ff_4_qn[1]));  // open: preset, reset, en
  or or_2 (or_2_out, and_4_out, and_5_out, and_6_out, and_7_out);
  T_Flip_Flop t_ff_4 (
    .clk(clock_1_out), .T(t_ff_4_qn[0]), .Q(t_ff_4_q[0]), .Qn(t_ff_4_qn[0]));  // open: preset, reset, en
  and and_4 (and_4_out, t_ff_4_q[3], t_ff_4_q[1]);
  and and_5 (and_5_out, t_ff_4_q[3], t_ff_4_qn[2], t_ff_4_q[0]);
  and and_6 (and_6_out, t_ff_4_q[2], t_ff_4_qn[1], t_ff_4_qn[0]);
  and and_7 (and_7_out, t_ff_4_qn[2], t_ff_4_q[1], t_ff_4_q[0]);
  Hex_Digit_Display hex_digit_display_1 (.value(t_ff_4_q));  // open: dp
  or or_3 (or_3_out, and_8_out, and_9_out, and_10_out, and_11_out, and_12_out);
  and and_8 (and_8_out, t_ff_4_q[3], t_ff_4_q[1], t_ff_4_q[0]);
  and and_9 (and_9_out, t_ff_4_q[3], t_ff_4_qn[1], t_ff_4_qn[0]);
  and and_10 (and_10_out, t_ff_4_q[2], t_ff_4_q[1], t_ff_4_q[0]);
  and and_11 (and_11_out, t_ff_4_qn[3], t_ff_4_qn[2], t_ff_4_q[1], t_ff_4_qn[0]);
  and and_12 (and_12_out, t_ff_4_qn[3], t_ff_4_qn[2], t_ff_4_qn[1], t_ff_4_q[0]);

  // Notes on the sheet:
  //   notQ
  //   Q
  //   notQ
  //   Q
  //   Q
  //   notQ
  //   notQ
  //   Q
  //   notQ
  //   Q
endmodule
