// Logisim project 2кр_Тимошенко.circ as structural Verilog: 1 circuit, main circuit main
module main (
);

  wire and_1_out, and_2_out, and_4_out, and_5_out, and_6_out, and_7_out, and_8_out, and_9_out, clock_1_out,
       or_1_out, or_2_out, or_3_out, or_4_out, undriven;
  wire [3:0] t_ff_4_q, t_ff_4_qn;

  Clock clock_1 (.out(clock_1_out));
  T_Flip_Flop t_ff_1 (
    .clk(clock_1_out), .T(or_1_out), .Q(t_ff_4_q[3]), .Qn(t_ff_4_qn[3]), .en(1'b1));  // open: preset, reset
  or or_1 (or_1_out, and_1_out, and_2_out);
  T_Flip_Flop t_ff_2 (
    .clk(clock_1_out), .T(or_2_out), .Q(t_ff_4_q[2]), .Qn(t_ff_4_qn[2]), .en(1'b1));  // open: preset, reset
  and and_1 (and_1_out, t_ff_4_qn[3], t_ff_4_q[2]);
  and and_2 (and_2_out, t_ff_4_q[3], t_ff_4_q[2], t_ff_4_q[1]);
  // AND_Gate and_3 has open pins: in0=undriven, in1=t_ff_4_qn[1], in2=t_ff_4_qn[0], out=open
  T_Flip_Flop t_ff_3 (
    .clk(clock_1_out), .T(or_3_out), .Q(t_ff_4_q[1]), .Qn(t_ff_4_qn[1]), .en(1'b1));  // open: preset, reset
  or or_2 (or_2_out, and_4_out, and_5_out);
  T_Flip_Flop t_ff_4 (
    .clk(clock_1_out), .T(or_4_out), .Q(t_ff_4_q[0]), .Qn(t_ff_4_qn[0]), .en(1'b1));  // open: preset, reset
  and and_4 (and_4_out, t_ff_4_q[1], t_ff_4_q[0]);
  and and_5 (and_5_out, t_ff_4_q[3], t_ff_4_qn[2]);
  Hex_Digit_Display hex_digit_display_1 (.value(t_ff_4_q));  // open: dp
  or or_3 (or_3_out, and_6_out, and_7_out);
  and and_6 (and_6_out, t_ff_4_q[3], t_ff_4_q[0]);
  and and_7 (and_7_out, t_ff_4_qn[2], t_ff_4_q[1]);
  or or_4 (or_4_out, and_8_out, and_9_out);
  and and_8 (and_8_out, t_ff_4_q[2], t_ff_4_q[1]);
  and and_9 (and_9_out, t_ff_4_qn[3], t_ff_4_qn[1], t_ff_4_q[0]);

  // Notes on the sheet:
  //   notQ
  //   Q
  //   notQ
  //   Q
  //   Q
  //   notQ
  //   notQ
  //   Q
  //   notQ
  //   Q
endmodule
